# Fritzing sketch screen (saved by Fritzing 0.9.9b)
breadboards: 1

parts:
  U1 = NodeMCU V1.0
  Part1 = LCD1602-I2C
  DispMod+ = KY-004 Key Switch Module [package="Breakout board"]
  Mod3 = KY-004 Key Switch Module [package="Breakout board"]
  Mod4 = KY-004 Key Switch Module [package="Breakout board"]
  R1 = Resistor [tolerance=±5% power=0.25 resistance=10k package=THT]

nets:
  N1: U1.D1, Part1.SCL
  N2: U1.D2, Part1.SDA
  N3: U1.D3, Mod3.S
  N4: U1.3V3, R1.Pin_0
  GND: U1.GND, Part1.GND, DispMod+.-, Mod3.-, Mod4.-
  N5: U1.D6, Mod4.S
  VIN: U1.Vin, Part1.VCC
  N6: U1.RST, DispMod+.S, R1.Pin_1

custom parts:
  NodeMCU V1.0: ESP8266 based NodeMCU
  LCD1602-I2C: A standard character display, usually with 2x16 characters. Comes in many colors with LCM1602 IIC attached.
  KY-004 Key Switch Module: Arduino Key Switch Module Keyes KY-004 is a push button that will output a high signal when pressed.
