# Fritzing sketch screen_db (saved by Fritzing 0.9.9b)
breadboards: 1

parts:
  U1 = NodeMCU V1.0
  RE1 = KY-040 Rotary encoder [package="Breakout board"]
  Part1 = LCD1602-I2C

nets:
  N1: U1.D1, Part1.SCL
  N2: U1.D2, Part1.SDA
  N3: U1.D3, RE1.CLK
  N4: U1.D4, RE1.DT
  3V3: U1.3V3, RE1.Vcc
  GND: U1.GND, RE1.GND, Part1.GND
  VIN: U1.Vin, Part1.VCC

custom parts:
  NodeMCU V1.0: ESP8266 based NodeMCU
  KY-040 Rotary encoder: KY-040 Rotary Encoder with switch on breakout borad from AZ Delivery
  LCD1602-I2C: A standard character display, usually with 2x16 characters. Comes in many colors with LCM1602 IIC attached.
